// Logisim project Projet_AdO.circ as structural Verilog: 27 circuits, main circuit main
module main (
);

  wire button_2_out, CLK, clock_1_out, or_1_out, PC_WAIT, RST, WRam;
  wire [1:0] SPSel, WSel;
  wire [2:0] alu_1_flags, MuxData;
  wire [3:0] stack_1_out_8, stack_1_out_9, stack_1_out_10;
  wire [5:0] OpCode;
  wire [9:0] valInstr_adrInstr;
  wire [15:0] ALU_OUT, bit_extender_1_out, bit_extender_2_out, multiplexer_1_out, PC, RAM_OUT, Stack_SP,
       Stack_SP_1, TEST_OUT;

  ROM #(.addrWidth(16), .dataWidth(16)) rom_1 (.addr(PC), .data({OpCode, valInstr_adrInstr}));  // open: sel
  assign bit_extender_1_out = {{6{1'b0}}, valInstr_adrInstr};  // Bit_Extender bit_extender_1
  Controller controller_1 (
    .OpCode(OpCode), .WSel(WSel), .PC_WAIT(PC_WAIT), .MuxData(MuxData), .WRam(WRam), .SPSel(SPSel),
    .STACK_SP(Stack_SP));
  assign bit_extender_2_out = {{6{1'b0}}, valInstr_adrInstr};  // Bit_Extender bit_extender_2
  // Probe on multiplexer_1_out
  Multiplexer #(.select(3), .width(16), .enable("false")) multiplexer_1 (
    .in0({16{1'b0}}), .in1(ALU_OUT), .in2(TEST_OUT), .in3(bit_extender_2_out), .in4(RAM_OUT), .in5(Stack_SP),
    .in6({16{1'b0}}), .in7({16{1'b0}}), .out(multiplexer_1_out), .sel(MuxData));
  // Probe on RAM_OUT
  RAM #(.addrWidth(16), .dataWidth(16), .bus("separate")) ram_1 (
    .addr(bit_extender_1_out), .din(Stack_SP), .data(RAM_OUT), .str(WRam), .clk(CLK), .clr(RST));  // open: sel, ld
  // Probe on SPSel
  // Probe on WSel
  Stack stack_1 (
    .Wsel(WSel), .CLK(CLK), .INPUT(multiplexer_1_out), .RESET_MEM(RST), .SPsel(SPSel), .MEM_SP(Stack_SP),
    .MEM_SP_1(Stack_SP_1), .out_10(stack_1_out_10), .out_9(stack_1_out_9), .out_8(stack_1_out_8));
  or or_1 (or_1_out, RST, PC_WAIT);
  // Probe on Stack_SP
  // Probe on Stack_SP_1
  // Probe on stack_1_out_10
  // Probe on stack_1_out_9
  // Probe on stack_1_out_8
  // Probe on ALU_OUT
  ALU alu_1 (.A(Stack_SP_1), .B(Stack_SP), .OpCode(OpCode), .C(ALU_OUT), .Flags(alu_1_flags));  // open: CBout
  // Probe on TEST_OUT
  tester tester_1 (.FLAGS(alu_1_flags), .OpCode(OpCode), .Q(TEST_OUT));
  \MàJ_PC  \màj_pc_1  (
    .AdrInstr(valInstr_adrInstr), .OpCode(OpCode), .TEST(Stack_SP), .CLK(CLK), .RESET(RST), .WAIT(or_1_out),
    .PC(PC));
  Button button_1 (.out(RST));
  Button button_2 (.out(button_2_out));
  Clock clock_1 (.out(clock_1_out));
  or or_2 (CLK, button_2_out, clock_1_out);

  // Notes on the sheet:
  //   THE FIFTH
  //   ROM
  //   RAM
  //   CONTROLLER
  //   STACK
  //   By Quentin GOMES DOS REIS & Kylian GERARD
  //   contents of rom_1 (hex, n*v repeats v):
  //   4405 5404 5000 6000 5c00 4400 3000 400b 4c00 4401 3810 5c00 4401 400 5404 c00 5800
  //   UpdatePC
  //   ALU & TESTER
  //   CONTROL PANEL
  //   NOTE: PRESS RESET BEFORE ANY
  //   START OR RESTART
  //   RESET
  //   CLOCK
endmodule

module _4bits_incr (
  input  [3:0] D,
  input  EN,
  output [3:0] out_3
);

  wire and_1_out, and_2_out, and_3_out, or_1_out, or_2_out, or_3_out, or_4_out, xor_1_out, xor_2_out,
       xor_3_out, xor_4_out;

  and and_1 (and_1_out, D[3], D[2], D[1], D[0]);
  and and_2 (and_2_out, D[1], D[0]);
  and and_3 (and_3_out, D[2], and_2_out);
  xor xor_1 (xor_1_out, 1'b1, D[0]);
  xor xor_2 (xor_2_out, D[0], D[1]);
  xor xor_3 (xor_3_out, and_2_out, D[2]);
  xor xor_4 (xor_4_out, and_3_out, D[3]);
  or or_1 (or_1_out, and_1_out, xor_1_out);
  and and_4 (out_3[0], or_1_out, EN);
  or or_2 (or_2_out, and_1_out, xor_2_out);
  and and_5 (out_3[1], or_2_out, EN);
  or or_3 (or_3_out, and_1_out, xor_3_out);
  and and_6 (out_3[2], or_3_out, EN);
  or or_4 (or_4_out, and_1_out, xor_4_out);
  and and_7 (out_3[3], or_4_out, EN);

  // Notes on the sheet:
  //   ENABLE OUTPUT
  //   4 BITS VALUE POSSIBLE TO AVOID
  //   REGISTER ERRORS
  //   WHEN AN OVERFLOW IS DETECTED
  //   RESULTING VALUE IS THE HIGHEST
endmodule

module _4bits_decr (
  input  [3:0] D,
  input  EN,
  output [3:0] out_3
);

  wire and_1_out, and_2_out, and_3_out, not_1_out, not_2_out, not_3_out, not_4_out, not_5_out, not_6_out,
       or_1_out, xor_1_out, xor_2_out, xor_3_out;

  not not_1 (not_1_out, D[0]);
  not not_2 (not_2_out, D[2]);
  not not_3 (not_3_out, EN);
  not not_4 (not_4_out, D[3]);
  not not_5 (not_5_out, D[1]);
  and and_1 (and_1_out, not_1_out, not_5_out, not_2_out, not_4_out);
  xor xor_1 (xor_1_out, not_1_out, D[1]);
  and and_2 (and_2_out, not_1_out, not_5_out);
  not not_6 (not_6_out, or_1_out);
  or or_1 (or_1_out, and_1_out, not_3_out);
  xor xor_2 (xor_2_out, and_2_out, D[2]);
  and and_3 (and_3_out, and_2_out, not_2_out);
  xor xor_3 (xor_3_out, and_3_out, D[3]);
  and and_4 (out_3[0], not_1_out, not_6_out);
  and and_5 (out_3[1], xor_1_out, not_6_out);
  and and_6 (out_3[2], xor_2_out, not_6_out);
  and and_7 (out_3[3], xor_3_out, not_6_out);

  // Notes on the sheet:
  //   ENABLE OUTPUT
  //   OUTPUT DISABLED AT THE LOWEST 4 BITS VALUE (0000)
endmodule

module _4bits_dmux (
  input  [3:0] D,
  output [3:0] Q0,
  output [3:0] Q1,
  output [3:0] Q2,
  output [3:0] Q3
);

  wire _00XX_out, _01XX_out, _10XX_out, _11XX_out, not_1_out, not_2_out, not_3_out, not_4_out, XX00_out,
       XX01_out, XX10_out, XX11_out;

  not not_1 (not_1_out, D[1]);
  not not_2 (not_2_out, D[2]);
  not not_3 (not_3_out, D[3]);
  not not_4 (not_4_out, D[0]);
  and XX00 (XX00_out, not_4_out, not_1_out);
  and XX01 (XX01_out, D[0], not_1_out);
  and XX10 (XX10_out, not_4_out, D[1]);
  and XX11 (XX11_out, D[0], D[1]);
  and _00XX (_00XX_out, not_2_out, not_3_out);
  and _01XX (_01XX_out, D[2], not_3_out);
  and _10XX (_10XX_out, not_2_out, D[3]);
  and _11XX (_11XX_out, D[2], D[3]);
  and and_1 (Q3[2], _11XX_out, XX10_out);
  and and_2 (Q3[3], _11XX_out, XX11_out);
  and and_3 (Q2[3], _10XX_out, XX11_out);
  and and_4 (Q3[0], _11XX_out, XX00_out);
  and and_5 (Q3[1], _11XX_out, XX01_out);
  and and_6 (Q2[2], _10XX_out, XX10_out);
  and and_7 (Q2[1], _10XX_out, XX01_out);
  and and_8 (Q2[0], _10XX_out, XX00_out);
  and and_9 (Q1[3], _01XX_out, XX11_out);
  and and_10 (Q1[2], _01XX_out, XX10_out);
  and and_11 (Q0[3], _00XX_out, XX11_out);
  and and_12 (Q1[1], _01XX_out, XX01_out);
  and and_13 (Q1[0], _01XX_out, XX00_out);
  and and_14 (Q0[2], _00XX_out, XX10_out);
  and and_15 (Q0[1], _00XX_out, XX01_out);
  and and_16 (Q0[0], _00XX_out, XX00_out);
endmodule

module _4bits_flowctrl (
  input  EN,
  input  [3:0] D,
  output [3:0] Q
);

  Multiplexer #(.width(4), .enable("false")) multiplexer_1 (.in0(4'b0000), .in1(D), .out(Q), .sel(EN));

  // Notes on the sheet:
  //   THIS MODULE JUST ACTS LIKE
  //   A 4BITS SWITCH
  //   IF EN = 1, ALL BITS FROM D PASS THROUGH SO Q = D 
  //   AND WHEN EN = 0, ALL BITS FROM D ARE BLOCKED SO Q = 0
endmodule

module Stack (
  input  [1:0] Wsel,
  input  CLK,
  input  [15:0] INPUT,
  input  RESET_MEM,
  input  [1:0] SPsel,
  output [15:0] MEM_SP,
  output [15:0] MEM_SP_1,
  output [3:0] out_8,
  output [3:0] out_9,
  output [3:0] out_10
);

  wire and_1_out, and_2_out, and_3_out, and_4_out, not_1_out, or_1_out;
  wire [3:0] multiplexer_1_out, n4bits_dmux_1_q0, R0_0, R0_1, R0_2, R0_3, R1_0, R1_1, R1_2, R1_3, W_0, W_1,
       W_2, W_3;
  wire [15:0] B0_Q0, B0_Q1, B1_Q0, B1_Q1, B2_Q0, B2_Q1, B3_Q0, B3_Q1, n16bits_register_1_debug_val,
       n16bits_register_1_q0, n16bits_register_1_q1, n16bits_register_2_debug_val, n16bits_register_2_q0,
       n16bits_register_2_q1, n16bits_register_3_debug_val, n16bits_register_3_q0, n16bits_register_3_q1,
       n16bits_register_4_debug_val, n16bits_register_4_q0, n16bits_register_4_q1,
       n16bits_register_5_debug_val, n16bits_register_5_q0, n16bits_register_5_q1,
       n16bits_register_6_debug_val, n16bits_register_6_q0, n16bits_register_6_q1,
       n16bits_register_7_debug_val, n16bits_register_7_q0, n16bits_register_7_q1,
       n16bits_register_8_debug_val, n16bits_register_8_q0, n16bits_register_8_q1,
       n16bits_register_9_debug_val, n16bits_register_9_q0, n16bits_register_9_q1,
       n16bits_register_10_debug_val, n16bits_register_10_q0, n16bits_register_10_q1,
       n16bits_register_11_debug_val, n16bits_register_11_q0, n16bits_register_11_q1,
       n16bits_register_12_debug_val, n16bits_register_12_q0, n16bits_register_12_q1,
       n16bits_register_13_debug_val, n16bits_register_13_q0, n16bits_register_13_q1,
       n16bits_register_14_debug_val, n16bits_register_14_q0, n16bits_register_14_q1,
       n16bits_register_15_debug_val, n16bits_register_15_q0, n16bits_register_15_q1,
       n16bits_register_16_debug_val, n16bits_register_16_q0, n16bits_register_16_q1;

  and and_1 (and_1_out, SPsel[0], SPsel[1]);
  and and_2 (and_2_out, SPsel[0], ~SPsel[1]);  // AND_Gate
  and and_3 (and_3_out, ~SPsel[0], ~SPsel[1]);  // AND_Gate
  or or_1 (or_1_out, and_3_out, RESET_MEM);
  _16bits_register u_16bits_register_1 (
    .READ_Q0(R0_1[3]), .READ_Q1(R1_1[3]), .CLK(CLK), .WRITE(W_1[3]), .RESET(RESET_MEM), .D(INPUT),
    .Q0(n16bits_register_1_q0), .Q1(n16bits_register_1_q1), .DEBUG_VAL(n16bits_register_1_debug_val));
  _16bits_register u_16bits_register_2 (
    .READ_Q0(R0_1[2]), .READ_Q1(R1_1[2]), .CLK(CLK), .WRITE(W_1[2]), .RESET(RESET_MEM), .D(INPUT),
    .Q0(n16bits_register_2_q0), .Q1(n16bits_register_2_q1), .DEBUG_VAL(n16bits_register_2_debug_val));
  _16bits_register u_16bits_register_3 (
    .READ_Q0(R0_1[1]), .READ_Q1(R1_1[1]), .CLK(CLK), .WRITE(W_1[1]), .RESET(RESET_MEM), .D(INPUT),
    .Q0(n16bits_register_3_q0), .Q1(n16bits_register_3_q1), .DEBUG_VAL(n16bits_register_3_debug_val));
  _16bits_register u_16bits_register_4 (
    .READ_Q0(R0_1[0]), .READ_Q1(R1_1[0]), .CLK(CLK), .WRITE(W_1[0]), .RESET(RESET_MEM), .D(INPUT),
    .Q0(n16bits_register_4_q0), .Q1(n16bits_register_4_q1), .DEBUG_VAL(n16bits_register_4_debug_val));
  and and_4 (and_4_out, Wsel[0], Wsel[1]);
  StackPointer stackpointer_1 (
    .PUSH(and_1_out), .POP(and_2_out), .CLK(CLK), .RESET(or_1_out), .SP_1(out_10), .SP(out_9), .SP_1_2(out_8));
  assign B1_Q1 = n16bits_register_4_q1 | n16bits_register_3_q1 | n16bits_register_2_q1 | n16bits_register_1_q1;  // OR_Gate Q1, 16 bits wide
  assign B1_Q0 = n16bits_register_4_q0 | n16bits_register_3_q0 | n16bits_register_2_q0 | n16bits_register_1_q0;  // OR_Gate Q0, 16 bits wide
  not not_1 (not_1_out, and_4_out);
  _4bits_dmux u_4bits_dmux_1 (.D(multiplexer_1_out), .Q3(W_3), .Q2(W_2), .Q1(W_1), .Q0(n4bits_dmux_1_q0));
  Multiplexer #(.select(2), .width(4), .disabled(0), .enable("false")) multiplexer_1 (
    .in0(out_9), .in1(out_10), .in2(out_8), .in3(4'b0000), .out(multiplexer_1_out), .sel(Wsel));
  _4bits_dmux u_4bits_dmux_2 (.D(out_9), .Q3(R0_3), .Q2(R0_2), .Q1(R0_1), .Q0(R0_0));
  _4bits_dmux u_4bits_dmux_3 (.D(out_8), .Q3(R1_3), .Q2(R1_2), .Q1(R1_1), .Q0(R1_0));
  _4bits_flowctrl u_4bits_flowctrl_1 (.EN(not_1_out), .D(n4bits_dmux_1_q0), .Q(W_0));
  _16bits_register u_16bits_register_5 (
    .READ_Q0(R0_2[3]), .READ_Q1(R1_2[3]), .CLK(CLK), .WRITE(W_2[3]), .RESET(RESET_MEM), .D(INPUT),
    .Q0(n16bits_register_5_q0), .Q1(n16bits_register_5_q1), .DEBUG_VAL(n16bits_register_5_debug_val));
  _16bits_register u_16bits_register_6 (
    .READ_Q0(R0_2[2]), .READ_Q1(R1_2[2]), .CLK(CLK), .WRITE(W_2[2]), .RESET(RESET_MEM), .D(INPUT),
    .Q0(n16bits_register_6_q0), .Q1(n16bits_register_6_q1), .DEBUG_VAL(n16bits_register_6_debug_val));
  _16bits_register u_16bits_register_7 (
    .READ_Q0(R0_2[1]), .READ_Q1(R1_2[1]), .CLK(CLK), .WRITE(W_2[1]), .RESET(RESET_MEM), .D(INPUT),
    .Q0(n16bits_register_7_q0), .Q1(n16bits_register_7_q1), .DEBUG_VAL(n16bits_register_7_debug_val));
  _16bits_register u_16bits_register_8 (
    .READ_Q0(R0_2[0]), .READ_Q1(R1_2[0]), .CLK(CLK), .WRITE(W_2[0]), .RESET(RESET_MEM), .D(INPUT),
    .Q0(n16bits_register_8_q0), .Q1(n16bits_register_8_q1), .DEBUG_VAL(n16bits_register_8_debug_val));
  assign B2_Q0 = n16bits_register_8_q0 | n16bits_register_7_q0 | n16bits_register_6_q0 | n16bits_register_5_q0;  // OR_Gate Q0_2, 16 bits wide
  assign B2_Q1 = n16bits_register_8_q1 | n16bits_register_7_q1 | n16bits_register_6_q1 | n16bits_register_5_q1;  // OR_Gate Q1_2, 16 bits wide
  _16bits_register u_16bits_register_9 (
    .READ_Q0(R0_0[3]), .READ_Q1(R1_0[3]), .CLK(CLK), .WRITE(W_0[3]), .RESET(RESET_MEM), .D(INPUT),
    .Q0(n16bits_register_9_q0), .Q1(n16bits_register_9_q1), .DEBUG_VAL(n16bits_register_9_debug_val));
  _16bits_register u_16bits_register_10 (
    .READ_Q0(R0_0[2]), .READ_Q1(R1_0[2]), .CLK(CLK), .WRITE(W_0[2]), .RESET(RESET_MEM), .D(INPUT),
    .Q0(n16bits_register_10_q0), .Q1(n16bits_register_10_q1), .DEBUG_VAL(n16bits_register_10_debug_val));
  _16bits_register u_16bits_register_11 (
    .READ_Q0(R0_0[1]), .READ_Q1(R1_0[1]), .CLK(CLK), .WRITE(W_0[1]), .RESET(RESET_MEM), .D(INPUT),
    .Q0(n16bits_register_11_q0), .Q1(n16bits_register_11_q1), .DEBUG_VAL(n16bits_register_11_debug_val));
  _16bits_register u_16bits_register_12 (
    .READ_Q0(R0_0[0]), .READ_Q1(R1_0[0]), .CLK(CLK), .WRITE(W_0[0]), .RESET(RESET_MEM), .D(INPUT),
    .Q0(n16bits_register_12_q0), .Q1(n16bits_register_12_q1), .DEBUG_VAL(n16bits_register_12_debug_val));
  assign B0_Q0 = n16bits_register_12_q0 | n16bits_register_11_q0 | n16bits_register_10_q0 | n16bits_register_9_q0;  // OR_Gate Q0_3, 16 bits wide
  assign B0_Q1 = n16bits_register_12_q1 | n16bits_register_11_q1 | n16bits_register_10_q1 | n16bits_register_9_q1;  // OR_Gate Q1_3, 16 bits wide
  _16bits_register u_16bits_register_13 (
    .READ_Q0(R0_3[3]), .READ_Q1(R1_3[3]), .CLK(CLK), .WRITE(W_3[3]), .RESET(RESET_MEM), .D(INPUT),
    .Q0(n16bits_register_13_q0), .Q1(n16bits_register_13_q1), .DEBUG_VAL(n16bits_register_13_debug_val));
  _16bits_register u_16bits_register_14 (
    .READ_Q0(R0_3[2]), .READ_Q1(R1_3[2]), .CLK(CLK), .WRITE(W_3[2]), .RESET(RESET_MEM), .D(INPUT),
    .Q0(n16bits_register_14_q0), .Q1(n16bits_register_14_q1), .DEBUG_VAL(n16bits_register_14_debug_val));
  _16bits_register u_16bits_register_15 (
    .READ_Q0(R0_3[1]), .READ_Q1(R1_3[1]), .CLK(CLK), .WRITE(W_3[1]), .RESET(RESET_MEM), .D(INPUT),
    .Q0(n16bits_register_15_q0), .Q1(n16bits_register_15_q1), .DEBUG_VAL(n16bits_register_15_debug_val));
  _16bits_register u_16bits_register_16 (
    .READ_Q0(R0_3[0]), .READ_Q1(R1_3[0]), .CLK(CLK), .WRITE(W_3[0]), .RESET(RESET_MEM), .D(INPUT),
    .Q0(n16bits_register_16_q0), .Q1(n16bits_register_16_q1), .DEBUG_VAL(n16bits_register_16_debug_val));
  assign MEM_SP = B0_Q0 | B1_Q0 | B2_Q0 | B3_Q0;  // OR_Gate Q0_4, 16 bits wide
  assign MEM_SP_1 = B0_Q1 | B1_Q1 | B2_Q1 | B3_Q1;  // OR_Gate Q1_4, 16 bits wide
  assign B3_Q0 = n16bits_register_16_q0 | n16bits_register_15_q0 | n16bits_register_14_q0 | n16bits_register_13_q0;  // OR_Gate Q0_5, 16 bits wide
  assign B3_Q1 = n16bits_register_16_q1 | n16bits_register_15_q1 | n16bits_register_14_q1 | n16bits_register_13_q1;  // OR_Gate Q1_5, 16 bits wide

  // Notes on the sheet:
  //   SPsel: pull=down
  //   00 - SP
  //   01 - SP-1
  //   10 - SP+1
  //   11 - NOTHING
  //   11 - PUSH
  //   01 - POP
  //   00 - RESET
  //   STACK
  //   TO DISABLE WRITE ON 0000
  //   WHEN WSel IS AT "NOTHING" STATE 
  //   WRITE
  //   READ_Q0
  //   READ_Q1
endmodule

module StackC (
  input  [15:0] INPUT,
  input  CLK,
  input  RESET_MEM,
  input  POP,
  input  PUSH,
  output [15:0] OUTPUT
);

  wire and_1_out, OLD_STATE_POP, or_1_out, register_2_q, SP___SP_1;
  wire [3:0] multiplexer_1_out, SP, SP_1, SP_1_t;

  or or_1 (or_1_out, POP, PUSH);
  Register #(.width(1)) register_1 (.D(POP), .en(or_1_out), .Q(OLD_STATE_POP), .clk(CLK), .clr(RESET_MEM));
  Register #(.width(1)) register_2 (.D(SP___SP_1), .Q(register_2_q), .clk(CLK), .clr(RESET_MEM));  // open: en
  StackPointer stackpointer_1 (
    .PUSH(PUSH), .POP(POP), .CLK(CLK), .RESET(RESET_MEM), .SP_1(SP_1_t), .SP(SP), .SP_1_2(SP_1));
  // Probe on SP
  // Probe on SP_1
  and and_1 (and_1_out, register_2_q, SP___SP_1);
  // Probe on SP_1_t
  Comparator #(.width(4), .mode("unsigned")) comparator_1 (.a(SP), .b(SP_1), .eq(SP___SP_1));  // open: gt, lt
  Multiplexer #(.width(4), .enable("false")) multiplexer_1 (.in0(SP), .in1(SP_1), .out(multiplexer_1_out), .sel(POP));
  // OR_Gate or_2 has open pins: in0=and_1_out, in1=PUSH, in2=OLD_STATE_POP, out=open
  RAM #(.addrWidth(4), .dataWidth(16), .bus("separate")) ram_1 (
    .addr(multiplexer_1_out), .din(INPUT), .data(OUTPUT), .str(PUSH), .clk(CLK), .ld(1'b1), .clr(RESET_MEM));  // open: sel

  // Notes on the sheet:
  //   TO SAVE THE PREVIOUS STATE OF POP INPUT
  //   STACK POINTER
  //   THAT PART IS NEEDED IN ORDER TO PROPERLY
  //   READ THE LAST 16BITS BLOCK OF THE STACK
  //   IF SP = SP+1
  //   OF THE STACK AND ALSO BECAUSE A
  //   A RAM MODULE IS USED TO REDUCE COMPLEXITY
  //   STACK HAS ALREADY BEEN CREATED BY HANDS
endmodule

module StackPointer (
  input  PUSH,
  input  POP,
  input  CLK,
  input  RESET,
  output [3:0] SP_1,
  output [3:0] SP,
  output [3:0] SP_1_2
);

  wire and_1_out, init, not_1_out, or_1_out, or_3_out;
  wire [3:0] multiplexer_1_out, n4bits_decr_1_out_3, n4bits_incr_1_out_3, or_2_out, register_1_q;

  or or_1 (or_1_out, POP, PUSH);
  _4bits_decr u_4bits_decr_1 (.D(SP), .EN(PUSH), .out_3(n4bits_decr_1_out_3));
  _4bits_incr u_4bits_incr_1 (.D(SP), .EN(POP), .out_3(n4bits_incr_1_out_3));
  assign or_2_out = n4bits_incr_1_out_3 | n4bits_decr_1_out_3;  // OR_Gate or_2, 4 bits wide
  and and_1 (and_1_out, init, ~or_1_out);  // AND_Gate
  Multiplexer #(.width(4), .disabled(0), .enable("false")) multiplexer_1 (
    .in0(or_2_out), .in1(4'b1111), .out(multiplexer_1_out), .sel(and_1_out));
  or or_3 (or_3_out, or_1_out, init);
  Register #(.width(4)) register_1 (.D(multiplexer_1_out), .en(or_3_out), .Q(register_1_q), .clk(CLK));  // open: clr
  Multiplexer #(.width(4), .disabled(0), .enable("false")) multiplexer_2 (
    .in0(register_1_q), .in1(4'b1111), .out(SP), .sel(init));
  S_R_Flip_Flop #(.trigger("falling")) s_r_ff_1 (
    .S(RESET), .clk(CLK), .R(not_1_out), .Q(init), .preset(RESET));  // open: Qn, reset, en
  not not_1 (not_1_out, RESET);
  _4bits_decr u_4bits_decr_2 (.D(SP), .EN(1'b1), .out_3(SP_1));
  _4bits_incr u_4bits_incr_2 (.D(SP), .EN(1'b1), .out_3(SP_1_2));

  // Notes on the sheet:
  //   PREVENT
  //   WHEN
  //   POP = 0
  //   DISABLE SR
  //   FLIP-FLOP TO
  //   UNWANTED
  //   MODIFICATIONS
  //   PUSH= 0 AND
  //   RESET CIRCUIT
  //   MODULES
  //   POINTER OVERFLOW IS
  //   HANDLED BY INCR AND DECR
endmodule

module ALU (
  input  [15:0] A,
  input  [15:0] B,
  input  [5:0] OpCode,
  output [15:0] C,
  output [2:0] Flags,
  output CBout
);

  wire B_OUT, C_OUT, EN_OUT, OF_ADD, OF_MUL, OF_SUB;
  wire [2:0] opcode_alu_1_q;
  wire [10:2] opcode_alu_1_q_2;
  wire [15:0] D, n16bits_add_1_q, n16bits_and_1_q, n16bits_div_1_q, n16bits_mul_1_q, n16bits_neg_1_q,
       n16bits_not_1_q, n16bits_or_1_q, n16bits_shl_1_q, n16bits_sra_1_q, n16bits_sud_1_q;

  _16bits_zero u_16bits_zero_1 (.A(D), .ZF(Flags[1]));
  BitSelector #(.width(16)) bitselector_1 (.in(D), .out(Flags[2]), .sel(4'b1111));
  OpCode_ALU opcode_alu_1 (
    .Op(OpCode), .Q({opcode_alu_1_q_2[10:4], opcode_alu_1_q[2], opcode_alu_1_q_2[2], opcode_alu_1_q[1:0]}),
    .EN(EN_OUT));
  Multiplexer #(.select(3), .disabled(0), .enable("false")) multiplexer_1 (
    .in0(1'b0), .in1(OF_ADD), .in2(OF_SUB), .in3(1'b0), .in4(OF_MUL), .in5(1'b0), .in6(1'b0), .in7(1'b0),
    .out(Flags[0]), .sel(opcode_alu_1_q));
  _16bits_add u_16bits_add_1 (.A(A), .B(B), .EN(opcode_alu_1_q[0]), .Q(n16bits_add_1_q), .C_OUT(OF_ADD), .OF(C_OUT));
  _16bits_sud u_16bits_sud_1 (.A(A), .B(B), .EN(opcode_alu_1_q[1]), .Q(n16bits_sud_1_q), .B_OUT(OF_SUB), .OF(B_OUT));
  _16bits_neg u_16bits_neg_1 (.A(A), .EN(opcode_alu_1_q_2[2]), .Q(n16bits_neg_1_q));
  _16bits_mul u_16bits_mul_1 (.A(A), .B(B), .EN(opcode_alu_1_q[2]), .Q(n16bits_mul_1_q), .OF(OF_MUL));
  _16bits_div u_16bits_div_1 (
    .A(A), .B(B), .EN_DIV(opcode_alu_1_q_2[4]), .EN_MOD(opcode_alu_1_q_2[5]), .Q(n16bits_div_1_q));
  _16bits_not u_16bits_not_1 (.A(A), .EN(opcode_alu_1_q_2[6]), .Q(n16bits_not_1_q));
  _16bits_and u_16bits_and_1 (.A(A), .B(B), .EN(opcode_alu_1_q_2[7]), .Q(n16bits_and_1_q));
  _16bits_or u_16bits_or_1 (.A(A), .B(B), .EN(opcode_alu_1_q_2[8]), .Q(n16bits_or_1_q));
  _16bits_sra u_16bits_sra_1 (.A(A), .B(B), .EN(opcode_alu_1_q_2[9]), .Q(n16bits_sra_1_q));
  _16bits_shl u_16bits_shl_1 (.A(A), .B(B), .EN(opcode_alu_1_q_2[10]), .Q(n16bits_shl_1_q));
  assign D = n16bits_add_1_q | n16bits_sud_1_q | n16bits_neg_1_q | n16bits_mul_1_q | n16bits_div_1_q | n16bits_not_1_q | n16bits_and_1_q | n16bits_or_1_q | n16bits_sra_1_q | n16bits_shl_1_q;  // OR_Gate or_1, 16 bits wide
  or or_2 (CBout, C_OUT, B_OUT);
  _16bits_flowctrl u_16bits_flowctrl_1 (.EN(EN_OUT), .D(D), .Q(C));

  // Other names for the same wires on the sheet: OF = Flags[0]; ZF = Flags[1]; SF = Flags[2]; Q[15:0] = C

  // Notes on the sheet:
  //   OVERFLOW FLAG
  //   ZEROFLAG
  //   SIGNFLAG
  //   FLAGS
endmodule

module OpCode_ALU (
  input  [5:0] Op,
  output [10:0] Q,
  output EN
);

  wire _00_out, _00XX_out, _01XX_out, _10XX_out, _11XX_out, EQ_out, GT_out, LT_out, not_1_out, not_2_out,
       not_3_out, not_4_out, or_1_out, or_2_out, SUB_out, XX00_out, XX01_out, XX10_out, XX11_out;

  not not_1 (not_1_out, Op[0]);
  not not_2 (not_2_out, Op[1]);
  not not_3 (not_3_out, Op[2]);
  not not_4 (not_4_out, Op[3]);
  and XX00 (XX00_out, not_1_out, not_2_out);
  and XX01 (XX01_out, Op[0], not_2_out);
  and XX10 (XX10_out, not_1_out, Op[1]);
  and XX11 (XX11_out, Op[0], Op[1]);
  and _00XX (_00XX_out, not_3_out, not_4_out);
  and _01XX (_01XX_out, Op[2], not_4_out);
  and _10XX (_10XX_out, not_3_out, Op[3]);
  and _11XX (_11XX_out, Op[2], Op[3]);
  and _00 (_00_out, ~Op[4], ~Op[5]);  // AND_Gate
  and GT (GT_out, _11XX_out, _00_out, XX01_out);
  and EQ (EQ_out, _11XX_out, _00_out, XX00_out);
  and LT (LT_out, _10XX_out, _00_out, XX11_out);
  and SRA (Q[10], _10XX_out, _00_out, XX10_out);
  or or_1 (or_1_out, GT_out, EQ_out, LT_out);
  or or_2 (or_2_out, ~_00_out, or_1_out);  // OR_Gate
  and AND (Q[7], _01XX_out, _00_out, XX11_out);
  and OR_3 (Q[8], _10XX_out, _00_out, XX00_out);
  and SHL (Q[9], _10XX_out, _00_out, XX01_out);
  and REM (Q[5], _01XX_out, _00_out, XX01_out);
  and NOT_5 (Q[6], _01XX_out, _00_out, XX10_out);
  and NEG (Q[2], _00XX_out, _00_out, XX10_out);
  and MUL (Q[3], _00XX_out, _00_out, XX11_out);
  and DIV (Q[4], _01XX_out, _00_out, XX00_out);
  not not_6 (EN, or_2_out);
  and SUB (SUB_out, _00XX_out, _00_out, XX01_out);
  and ADD (Q[0], _00XX_out, _00_out, XX00_out);
  or or_4 (Q[1], or_1_out, SUB_out);
endmodule

module _16bits_flowctrl (
  input  EN,
  input  [15:0] D,
  output [15:0] Q
);

  Multiplexer #(.width(16), .enable("false")) multiplexer_1 (.in0({16{1'b0}}), .in1(D), .out(Q), .sel(EN));

  // Notes on the sheet:
  //   THIS MODULE JUST ACTS LIKE
  //   A 16BITS SWITCH
  //   IF EN = 1, ALL BITS FROM D PASS THROUGH SO Q = D 
  //   AND WHEN EN = 0, ALL BITS FROM D ARE BLOCKED SO Q = 0
endmodule

module _16bits_register (
  input  READ_Q0,
  input  READ_Q1,
  input  CLK,
  input  WRITE,
  input  RESET,
  input  [15:0] D,
  output [15:0] Q0,
  output [15:0] Q1,
  output [15:0] DEBUG_VAL
);

  Register #(.width(16)) register_1 (.D(D), .en(WRITE), .Q(DEBUG_VAL), .clk(CLK), .clr(RESET));
  _16bits_flowctrl u_16bits_flowctrl_1 (.EN(READ_Q0), .D(DEBUG_VAL), .Q(Q0));
  _16bits_flowctrl u_16bits_flowctrl_2 (.EN(READ_Q1), .D(DEBUG_VAL), .Q(Q1));

  // Notes on the sheet:
  //   RESET: pull=down
  //   CLK: pull=down
  //   Q0: pull=down
  //   Q1: pull=down
  //   D: pull=down
  //   READ_Q0: pull=down
  //   WRITE: pull=down
  //   DEBUG_VAL: pull=down
  //   READ_Q1: pull=down
  //   WRITE ENABLE
  //   READ BUS (Q0 OR Q1)
endmodule

module \MàJ_PC  (
  input  [9:0] AdrInstr,
  input  [5:0] OpCode,
  input  [15:0] TEST,
  input  CLK,
  input  RESET,
  input  WAIT,
  output [15:0] PC
);

  wire _JMP, CALL, CALL_C0, CALL_C1, CALL_C2, JMP, JMPF, JMPF_out, JMPT, JMPT_out, NEG_TEST, not_2_out,
       or_2_out, or_3_out, register_1_q, register_2_q, register_3_q, RET, TEST_t;
  wire [15:0] AdrInstr_t, multiplexer_1_out, multiplexer_2_out, PC_1, STACK_OUT;

  not not_1 (TEST_t, NEG_TEST);
  _16bits_zero u_16bits_zero_1 (.A(TEST), .ZF(NEG_TEST));
  assign AdrInstr_t = {{6{1'b0}}, AdrInstr};  // Bit_Extender bit_extender_1
  and u_JMP (JMP, ~OpCode[0], OpCode[1], OpCode[2], OpCode[3], ~OpCode[4], ~OpCode[5]);  // AND_Gate
  and u_JMPT (JMPT_out, OpCode[0], OpCode[1], OpCode[2], OpCode[3], ~OpCode[4], ~OpCode[5]);  // AND_Gate
  and u_JMPF (JMPF_out, ~OpCode[0], ~OpCode[1], ~OpCode[2], ~OpCode[3], OpCode[4], ~OpCode[5]);  // AND_Gate
  and u_CALL (CALL, OpCode[0], ~OpCode[1], OpCode[2], ~OpCode[3], OpCode[4], ~OpCode[5]);  // AND_Gate
  and u_RET (RET, ~OpCode[0], OpCode[1], OpCode[2], ~OpCode[3], OpCode[4], ~OpCode[5]);  // AND_Gate
  Adder #(.width(16)) adder_1 (.a(16'h1), .b(PC), .out(PC_1));  // open: cin, cout
  and and_1 (JMPT, TEST_t, JMPT_out);
  and and_2 (JMPF, NEG_TEST, JMPF_out);
  and and_3 (CALL_C0, CALL, ~register_1_q);  // AND_Gate
  Register #(.width(1)) register_1 (.D(CALL), .Q(register_1_q), .clk(CLK), .clr(or_2_out));  // open: en
  and and_4 (CALL_C1, CALL, register_1_q, ~register_2_q);  // AND_Gate
  or or_1 (_JMP, JMP, JMPT, JMPF, CALL_C2);
  Register #(.width(1)) register_2 (.D(register_1_q), .Q(register_2_q), .clk(CLK), .clr(or_2_out));  // open: en
  Register #(.width(1)) register_3 (.D(register_2_q), .Q(register_3_q), .clk(CLK), .clr(or_2_out));  // open: en
  or or_2 (or_2_out, register_3_q, RESET);
  and and_5 (CALL_C2, CALL, register_2_q);
  StackC stackc_1 (.INPUT(PC_1), .CLK(CLK), .RESET_MEM(RESET), .POP(RET), .PUSH(CALL_C1), .OUTPUT(STACK_OUT));
  // Probe on PC
  Multiplexer #(.width(16), .enable("false")) multiplexer_1 (
    .in0(PC_1), .in1(STACK_OUT), .out(multiplexer_1_out), .sel(RET));
  Multiplexer #(.width(16), .enable("false")) multiplexer_2 (
    .in0(multiplexer_1_out), .in1(AdrInstr_t), .out(multiplexer_2_out), .sel(_JMP));
  not not_2 (not_2_out, or_3_out);
  or or_3 (or_3_out, CALL_C0, CALL_C1, WAIT);
  // Probe on PC
  PC u_pc_1 (.D(multiplexer_2_out), .EN(not_2_out), .CLK(CLK), .RESET(RESET), .O(PC));

  // Other names for the same wires on the sheet: PC_OUT[15:0] = PC; PC_OUTPUT[15:0] = PC

  // Notes on the sheet:
  //   OpCode: pull=down
  //   OPERATION CALL ON 3 CLOCK CYCLES
  //   CALL CYCLES
endmodule

module PC (
  input  [15:0] D,
  input  EN,
  input  CLK,
  input  RESET,
  output [15:0] O
);

  Register #(.width(16)) register_1 (.D(D), .en(EN), .Q(O), .clk(CLK), .clr(RESET));
endmodule

module tester (
  input  [2:0] FLAGS,
  input  [5:0] OpCode,
  output [15:0] Q
);

  wire and_1_out, and_2_out, and_3_out, and_4_out, eq_out, gt_out, lt_out, or_1_out, or_2_out;

  and lt (lt_out, OpCode[0], OpCode[1], ~OpCode[2], OpCode[3], ~OpCode[4], ~OpCode[5]);  // AND_Gate
  and eq (eq_out, ~OpCode[0], ~OpCode[1], OpCode[2], OpCode[3], ~OpCode[4], ~OpCode[5]);  // AND_Gate
  and gt (gt_out, OpCode[0], ~OpCode[1], OpCode[2], OpCode[3], ~OpCode[4], ~OpCode[5]);  // AND_Gate
  and and_1 (and_1_out, FLAGS[2], lt_out);
  and and_2 (and_2_out, FLAGS[1], eq_out);
  and and_3 (and_3_out, ~FLAGS[2], gt_out);  // AND_Gate
  or or_1 (or_1_out, lt_out, eq_out, gt_out);
  or or_2 (or_2_out, and_1_out, and_2_out, and_3_out);
  and and_4 (and_4_out, or_2_out, or_1_out);
  assign Q = {{15{and_4_out}}, and_4_out};  // Bit_Extender bit_extender_1

  // Notes on the sheet:
  //   FLAGS: pull=down
  //   0 - OF
  //   1 - ZF
  //   2 - SF
endmodule

module Controller (
  input  [15:0] STACK_SP,
  input  [5:0] OpCode,
  output [1:0] SPSel,
  output [1:0] WSel,
  output PC_WAIT,
  output [2:0] MuxData,
  output WRam
);

  wire ALU, and_1_out, and_3_out, and_5_out, and_7_out, and_9_out, and_11_out, and_13_out, and_17_out,
       and_18_out, and_19_out, and_20_out, call_adr, DUP, jmp, jmpf, jmpt, NEG_NOT, NEG_TEST, not_1_out,
       not_2_out, or_1_out, or_2_out, or_3_out, or_4_out, or_5_out, or_6_out, or_8_out, or_9_out, OTH_ALU,
       POP, PUSH_adr, PUSH_val, ret, TEST;
  wire [1:0] multiplexer_1_out, multiplexer_2_out, multiplexer_5_out, multiplexer_6_out, multiplexer_8_out;
  wire [2:0] multiplexer_3_out, multiplexer_4_out, multiplexer_7_out, multiplexer_9_out;
  wire [3:0] demultiplexer_1_out0, demultiplexer_1_out1;

  _16bits_zero u_16bits_zero_1 (.A(STACK_SP), .ZF(NEG_TEST));
  Demultiplexer #(.width(4), .disabled(0)) demultiplexer_1 (
    .out0(demultiplexer_1_out0), .out1(demultiplexer_1_out1), .in(OpCode[3:0]), .sel(OpCode[4]),
    .en(not_1_out));
  not not_1 (not_1_out, OpCode[5]);
  not not_2 (not_2_out, NEG_TEST);
  and and_1 (and_1_out, demultiplexer_1_out1[0], ~demultiplexer_1_out1[1]);  // AND_Gate
  and and_2 (PUSH_val, and_1_out, and_5_out);
  and and_3 (and_3_out, ~demultiplexer_1_out1[0], demultiplexer_1_out1[1]);  // AND_Gate
  and and_4 (PUSH_adr, and_3_out, and_5_out);
  and and_5 (and_5_out, ~demultiplexer_1_out1[2], ~demultiplexer_1_out1[3]);  // AND_Gate
  and and_6 (POP, and_5_out, and_7_out);
  and and_7 (and_7_out, demultiplexer_1_out1[0], demultiplexer_1_out1[1]);
  and and_8 (DUP, and_7_out, and_9_out);
  and and_9 (and_9_out, demultiplexer_1_out1[2], ~demultiplexer_1_out1[3]);  // AND_Gate
  and and_10 (WRam, and_9_out, and_11_out);
  and and_11 (and_11_out, ~demultiplexer_1_out1[0], ~demultiplexer_1_out1[1]);  // AND_Gate
  and and_12 (PC_WAIT, and_11_out, and_13_out);
  and and_13 (and_13_out, ~demultiplexer_1_out1[2], demultiplexer_1_out1[3]);  // AND_Gate
  and and_14 (jmpt, ~demultiplexer_1_out1[0], ~demultiplexer_1_out1[1], OpCode[4], ~demultiplexer_1_out1[2], ~demultiplexer_1_out1[3]);  // AND_Gate
  and and_15 (call_adr, demultiplexer_1_out1[0], ~demultiplexer_1_out1[1], OpCode[4], demultiplexer_1_out1[2], ~demultiplexer_1_out1[3]);  // AND_Gate
  and and_16 (ret, ~demultiplexer_1_out1[0], demultiplexer_1_out1[1], OpCode[4], demultiplexer_1_out1[2], ~demultiplexer_1_out1[3]);  // AND_Gate
  and and_17 (and_17_out, demultiplexer_1_out0[1], demultiplexer_1_out0[2], demultiplexer_1_out0[3]);
  and and_18 (and_18_out, demultiplexer_1_out0[0], demultiplexer_1_out0[1], ~demultiplexer_1_out0[2]);  // AND_Gate
  or or_1 (or_1_out, and_18_out, and_19_out);
  and and_19 (and_19_out, ~demultiplexer_1_out0[1], demultiplexer_1_out0[2]);  // AND_Gate
  or or_2 (or_2_out, demultiplexer_1_out0[0], ~demultiplexer_1_out0[1], demultiplexer_1_out0[3]);  // OR_Gate
  and and_20 (and_20_out, ~demultiplexer_1_out0[0], demultiplexer_1_out0[1], ~demultiplexer_1_out0[3]);  // AND_Gate
  and and_21 (jmp, ~demultiplexer_1_out0[0], demultiplexer_1_out0[1], ~OpCode[4], demultiplexer_1_out0[2], demultiplexer_1_out0[3]);  // AND_Gate
  and and_22 (jmpf, demultiplexer_1_out0[0], demultiplexer_1_out0[1], ~OpCode[4], demultiplexer_1_out0[2], demultiplexer_1_out0[3]);  // AND_Gate
  and and_23 (TEST, or_1_out, demultiplexer_1_out0[3]);
  and and_24 (OTH_ALU, ~TEST, ~and_17_out, ~OpCode[4], or_2_out);  // AND_Gate
  and and_25 (NEG_NOT, ~and_17_out, and_20_out);  // AND_Gate
  Multiplexer #(.width(2), .disabled(0), .enable("false")) multiplexer_1 (
    .in0(2'b11), .in1(2'b11), .out(multiplexer_1_out), .sel(or_3_out));
  or or_3 (or_3_out, PUSH_val, PUSH_adr, DUP);
  Multiplexer #(.width(2), .disabled(0), .enable("false")) multiplexer_2 (
    .in0(2'b11), .in1(2'b11), .out(multiplexer_2_out), .sel(or_4_out));
  or or_4 (or_4_out, jmp, jmpt, jmpf, POP, WRam, call_adr, ret, PC_WAIT);
  Multiplexer #(.width(3), .disabled(0), .enable("false")) multiplexer_3 (
    .in0(3'b000), .in1(3'b001), .out(multiplexer_3_out), .sel(ALU));
  or or_5 (or_5_out, jmp, call_adr, NEG_NOT, ret, PC_WAIT);
  or or_6 (or_6_out, OTH_ALU, TEST);
  Multiplexer #(.width(3), .disabled(0), .enable("false")) multiplexer_4 (
    .in0(multiplexer_3_out), .in1(3'b010), .out(multiplexer_4_out), .sel(TEST));
  or or_7 (ALU, OTH_ALU, NEG_NOT);
  Multiplexer #(.width(2), .disabled(0), .enable("false")) multiplexer_5 (
    .in0(multiplexer_1_out), .in1(2'b10), .out(multiplexer_5_out), .sel(or_5_out));
  Multiplexer #(.width(2), .disabled(0), .enable("false")) multiplexer_6 (
    .in0(multiplexer_2_out), .in1(2'b10), .out(multiplexer_6_out), .sel(or_6_out));
  Multiplexer #(.width(3), .disabled(0), .enable("false")) multiplexer_7 (
    .in0(multiplexer_4_out), .in1(3'b011), .out(multiplexer_7_out), .sel(PUSH_val));
  or or_8 (or_8_out, OTH_ALU, TEST, jmpt, jmpf, POP, WRam);
  Multiplexer #(.width(2), .disabled(0), .enable("false")) multiplexer_8 (
    .in0(multiplexer_6_out), .in1(2'b01), .out(multiplexer_8_out), .sel(or_9_out));
  or or_9 (or_9_out, DUP, PUSH_adr, PUSH_val);
  Multiplexer #(.width(3), .disabled(0), .enable("false")) multiplexer_9 (
    .in0(multiplexer_7_out), .in1(3'b100), .out(multiplexer_9_out), .sel(PUSH_adr));
  Multiplexer #(.width(3), .disabled(0), .enable("false")) multiplexer_10 (
    .in0(multiplexer_9_out), .in1(3'b101), .out(MuxData), .sel(DUP));
  Multiplexer #(.width(2), .disabled(0), .enable("false")) multiplexer_11 (
    .in0(multiplexer_5_out), .in1(2'b01), .out(SPSel), .sel(or_8_out));
  Multiplexer #(.width(2), .disabled(0), .enable("false")) multiplexer_12 (
    .in0(multiplexer_8_out), .in1(2'b00), .out(WSel), .sel(NEG_NOT));

  // Other names for the same wires on the sheet: HALT = PC_WAIT; _01XXXX = OpCode[4]; POP_adr = WRam; stack_top = DUP;
  //   valInstr = PUSH_val; valRam = PUSH_adr

  // Notes on the sheet:
  //   01XXXX
  //   00XXXX
  //   push val
  //   push [adr]
  //   pop
  //   dup
  //   pop[adr]
  //   halt
  //   jmpt
  //   call adr
  //   ret
  //   jmp
  //   jmpf
  //   neg \ not
  //   lt \ eq \ gt
  //   or \ shl \ sra
  //   add \ sub \ mul \ div \ rem \ and
  //   MuxData
  //   000 - Disable
  //   001 - ALU
  //   010 - TESTER
  //   011 - valInstr
  //   3 Select Bits
  //   100 - valRam
  //   101 - stack[top]
  //   110 - Not Used
  //   111 - Not Used
  //   ONLY ENABLED IN MULTICYCLES
  //   INSTRUCTIONS OR ON A HALT
  //   CONTROL RAM WRITING
endmodule

module _16bits_add (
  input  [15:0] A,
  input  [15:0] B,
  input  EN,
  output [15:0] Q,
  output C_OUT,
  output OF
);

  wire adder_1_cout, and_1_out, and_2_out, and_3_out, and_4_out, bitselector_1_out, bitselector_2_out,
       bitselector_3_out, or_1_out;
  wire [15:0] adder_1_out;

  Adder #(.width(16)) adder_1 (.a(A), .b(B), .out(adder_1_out), .cout(adder_1_cout));  // open: cin
  BitSelector #(.width(16)) bitselector_1 (.in(adder_1_out), .out(bitselector_1_out), .sel(4'b1111));
  BitSelector #(.width(16)) bitselector_2 (.in(A), .out(bitselector_2_out), .sel(4'b1111));
  BitSelector #(.width(16)) bitselector_3 (.in(B), .out(bitselector_3_out), .sel(4'b1111));
  and and_1 (and_1_out, bitselector_1_out, and_2_out);
  and and_2 (and_2_out, ~bitselector_2_out, ~bitselector_3_out);  // AND_Gate
  and and_3 (and_3_out, ~bitselector_1_out, and_4_out);  // AND_Gate
  and and_4 (and_4_out, bitselector_2_out, bitselector_3_out);
  _16bits_flowctrl u_16bits_flowctrl_1 (.EN(EN), .D(adder_1_out), .Q(Q));
  or or_1 (or_1_out, and_1_out, and_3_out);
  and and_5 (C_OUT, EN, adder_1_cout);
  and and_6 (OF, EN, or_1_out);

  // Notes on the sheet:
  //   SELECTION OF
  //   THE HIGHEST
  //   WEIGHT BIT
  //   OVERFLOW DETECTION
endmodule

module _16bits_sud (
  input  [15:0] A,
  input  [15:0] B,
  input  EN,
  output [15:0] Q,
  output B_OUT,
  output OF
);

  wire and_2_out, and_3_out, and_4_out, and_out, bitselector_1_out, bitselector_2_out, bitselector_3_out,
       or_1_out, subtractor_1_bout;
  wire [15:0] subtractor_1_out;

  Subtractor #(.width(16)) subtractor_1 (.a(A), .b(B), .out(subtractor_1_out), .bout(subtractor_1_bout));  // open: bin
  BitSelector #(.width(16)) bitselector_1 (.in(A), .out(bitselector_1_out), .sel(4'b1111));
  BitSelector #(.width(16)) bitselector_2 (.in(B), .out(bitselector_2_out), .sel(4'b1111));
  BitSelector #(.width(16)) bitselector_3 (.in(subtractor_1_out), .out(bitselector_3_out), .sel(4'b1111));
  and \and  (and_out, ~bitselector_1_out, bitselector_2_out);  // AND_Gate
  and and_2 (and_2_out, bitselector_1_out, ~bitselector_2_out);  // AND_Gate
  and and_3 (and_3_out, bitselector_3_out, and_out);
  or or_1 (or_1_out, and_3_out, and_4_out);
  and and_4 (and_4_out, ~bitselector_3_out, and_2_out);  // AND_Gate
  _16bits_flowctrl u_16bits_flowctrl_1 (.EN(EN), .D(subtractor_1_out), .Q(Q));
  and and_5 (B_OUT, EN, subtractor_1_bout);
  and and_6 (OF, or_1_out, EN);

  // Notes on the sheet:
  //   SELECTION OF
  //   THE HIGHEST
  //   WEIGHT BIT
  //   OVERFLOW DETECTION
endmodule

module _16bits_neg (
  input  [15:0] A,
  input  EN,
  output [15:0] Q
);

  wire [15:0] negator_1_out;

  Negator #(.width(16)) negator_1 (.in(A), .out(negator_1_out));
  _16bits_flowctrl u_16bits_flowctrl_1 (.EN(EN), .D(negator_1_out), .Q(Q));
endmodule

module _16bits_mul (
  input  [15:0] A,
  input  [15:0] B,
  input  EN,
  output [15:0] Q,
  output OF
);

  wire and_1_out, and_2_out, and_3_out, and_4_out, bitselector_1_out, bitselector_2_out, bitselector_3_out,
       or_1_out;
  wire [15:0] multiplier_1_out;

  BitSelector #(.width(16)) bitselector_1 (.in(A), .out(bitselector_1_out), .sel(4'b1111));
  Multiplier #(.width(16)) multiplier_1 (.a(A), .b(B), .out(multiplier_1_out));  // open: cin, cout
  BitSelector #(.width(16)) bitselector_2 (.in(B), .out(bitselector_2_out), .sel(4'b1111));
  BitSelector #(.width(16)) bitselector_3 (.in(multiplier_1_out), .out(bitselector_3_out), .sel(4'b1111));
  and and_1 (and_1_out, bitselector_1_out, bitselector_2_out, bitselector_3_out);
  and and_2 (and_2_out, ~bitselector_1_out, ~bitselector_2_out, bitselector_3_out);  // AND_Gate
  and and_3 (and_3_out, ~bitselector_1_out, ~bitselector_3_out);  // AND_Gate
  and and_4 (and_4_out, bitselector_1_out, ~bitselector_2_out, ~bitselector_3_out);  // AND_Gate
  _16bits_flowctrl u_16bits_flowctrl_1 (.EN(EN), .D(multiplier_1_out), .Q(Q));
  or or_1 (or_1_out, and_1_out, and_2_out, and_3_out, and_4_out);
  and and_5 (OF, EN, or_1_out);

  // Notes on the sheet:
  //   OVERFLOW
  //   DETECTION
endmodule

module _16bits_div (
  input  [15:0] A,
  input  [15:0] B,
  input  EN_DIV,
  input  EN_MOD,
  output [15:0] Q
);

  wire [15:0] divider_1_out, divider_1_rem, n16bits_flowctrl_1_q, n16bits_flowctrl_2_q;

  Divider #(.width(16)) divider_1 (.a(A), .b(B), .out(divider_1_out), .rem(divider_1_rem));  // open: upper
  _16bits_flowctrl u_16bits_flowctrl_1 (.EN(EN_DIV), .D(divider_1_out), .Q(n16bits_flowctrl_1_q));
  assign Q = n16bits_flowctrl_1_q | n16bits_flowctrl_2_q;  // OR_Gate or_1, 16 bits wide
  _16bits_flowctrl u_16bits_flowctrl_2 (.EN(EN_MOD), .D(divider_1_rem), .Q(n16bits_flowctrl_2_q));
endmodule

module _16bits_not (
  input  [15:0] A,
  input  EN,
  output [15:0] Q
);

  wire [15:0] not_1_out;

  assign not_1_out = ~A;  // NOT_Gate not_1, 16 bits wide
  _16bits_flowctrl u_16bits_flowctrl_1 (.EN(EN), .D(not_1_out), .Q(Q));
endmodule

module _16bits_and (
  input  [15:0] A,
  input  [15:0] B,
  input  EN,
  output [15:0] Q
);

  wire [15:0] and_1_out;

  assign and_1_out = A & B;  // AND_Gate and_1, 16 bits wide
  _16bits_flowctrl u_16bits_flowctrl_1 (.EN(EN), .D(and_1_out), .Q(Q));
endmodule

module _16bits_or (
  input  [15:0] A,
  input  [15:0] B,
  input  EN,
  output [15:0] Q
);

  wire [15:0] or_1_out;

  assign or_1_out = A | B;  // OR_Gate or_1, 16 bits wide
  _16bits_flowctrl u_16bits_flowctrl_1 (.EN(EN), .D(or_1_out), .Q(Q));
endmodule

module _16bits_sra (
  input  [15:0] A,
  input  [15:0] B,
  input  EN,
  output [15:0] Q
);

  wire [15:0] shifter_1_out;

  Shifter #(.width(16), .shift("ar")) shifter_1 (.in(A), .\dist (B[3:0]), .out(shifter_1_out));
  _16bits_flowctrl u_16bits_flowctrl_1 (.EN(EN), .D(shifter_1_out), .Q(Q));
endmodule

module _16bits_shl (
  input  [15:0] A,
  input  [15:0] B,
  input  EN,
  output [15:0] Q
);

  wire [15:0] shifter_1_out;

  Shifter #(.width(16)) shifter_1 (.in(A), .\dist (B[3:0]), .out(shifter_1_out));
  _16bits_flowctrl u_16bits_flowctrl_1 (.EN(EN), .D(shifter_1_out), .Q(Q));
endmodule

module _16bits_zero (
  input  [15:0] A,
  output ZF
);

  wire bitfinder_1_found;

  not not_1 (ZF, bitfinder_1_found);
  BitFinder #(.width(16), .\type ("high1")) bitfinder_1 (.in(A), .found(bitfinder_1_found));  // open: index

  // Notes on the sheet:
  //   ZERO FLAG MODULE
  //   JUST CHECK IF ANY BIT IS AT 1
  //   ELSE THE OUTPUT IS 1
  //   IF AT LEAST ONE BIT IS AT 1 THE OUTPUT IS 0
endmodule
